// Logisim project lab3circuit.circ as structural Verilog: 1 circuit, main circuit main
module main (
  input  A2,
  input  A1,
  input  A0,
  input  B2,
  input  B1,
  input  B0,
  output A_B,
  output A_B_2,
  output A_B_3
);

  wire and_1_out, and_2_out, and_3_out, and_4_out, and_5_out, and_6_out, and_7_out, and_8_out, and_9_out,
       and_10_out, and_11_out, and_12_out, and_13_out, and_14_out, and_15_out, and_16_out, and_17_out,
       and_18_out, not_1_out, not_2_out, not_3_out, not_4_out, or_1_out, or_2_out, or_3_out, or_4_out,
       or_5_out, or_6_out, or_7_out, or_8_out, or_9_out, or_10_out;

  not not_1 (not_1_out, A0);
  not not_2 (not_2_out, B2);
  not not_3 (not_3_out, B1);
  not not_4 (not_4_out, B0);
  and and_1 (and_1_out, A0, not_2_out, not_3_out, not_4_out);
  and and_2 (and_2_out, not_3_out, not_2_out);
  and and_3 (and_3_out, A0, not_2_out, B1, not_4_out);
  and and_4 (and_4_out, A0, B2, not_3_out, not_4_out);
  and and_5 (and_5_out, A0, B2, B1, not_4_out);
  and and_6 (and_6_out, not_1_out, not_2_out, not_3_out, B0);
  and and_7 (and_7_out, not_1_out, not_2_out, B0, B1);
  and and_8 (and_8_out, not_1_out, B2, not_3_out, B0);
  and and_9 (and_9_out, B2, B1);
  and and_10 (and_10_out, not_1_out, B2, B1, B0);
  and and_11 (and_11_out, not_1_out, not_2_out, not_3_out, not_4_out);
  and and_12 (and_12_out, A0, not_2_out, not_3_out, B0);
  and and_13 (and_13_out, A0, not_2_out, B1, B0);
  and and_14 (and_14_out, not_1_out, not_2_out, B1, not_4_out);
  and and_15 (and_15_out, not_1_out, B2, not_3_out, not_4_out);
  and and_16 (and_16_out, A0, B2, not_3_out, B0);
  and and_17 (and_17_out, A0, B2, B1, B0);
  and and_18 (and_18_out, not_1_out, B2, B1, not_4_out);
  or or_1 (or_1_out, and_2_out, and_3_out);
  or or_2 (or_2_out, and_4_out, not_2_out);
  or or_3 (or_3_out, and_5_out, not_3_out, not_2_out);
  or or_4 (or_4_out, and_6_out, B2, B1);
  or or_5 (or_5_out, and_7_out, B2);
  or or_6 (or_6_out, and_8_out, and_9_out);
  or or_7 (or_7_out, and_11_out, and_12_out);
  or or_8 (or_8_out, and_13_out, and_14_out);
  or or_9 (or_9_out, and_15_out, and_16_out);
  or or_10 (or_10_out, and_17_out, and_18_out);
  Multiplexer #(.select(2)) multiplexer_1 (
    .in0(and_1_out), .in1(or_1_out), .in2(or_2_out), .in3(or_3_out), .out(A_B), .sel({A2, A1}));
  Multiplexer #(.select(2)) multiplexer_2 (
    .in0(or_4_out), .in1(or_5_out), .in2(or_6_out), .in3(and_10_out), .out(A_B_2), .sel({A2, A1}));
  Multiplexer #(.select(2)) multiplexer_3 (
    .in0(or_7_out), .in1(or_8_out), .in2(or_9_out), .in3(or_10_out), .out(A_B_3), .sel({A2, A1}));

  // Notes on the sheet:
  //   A>B
  //   A<B
  //   A=B
endmodule
